# Fritzing sketch schematic (saved by Fritzing 0.9.3b)
breadboards: 1

parts:
  Arduino = Arduino Uno (Rev3)
  Temperature_Sensor = TMP36 Temperature Sensor [thermistor_type=NTC package="TO92 [THT]"]
  Select_Button = Pushbutton [package="[THT]"]
  Up_Button = Pushbutton [package="[THT]"]
  Down_Button = Pushbutton [package="[THT]"]
  R1 = Resistor [tolerance=±5% resistance=1k package=THT]
  R2 = Resistor [tolerance=±5% resistance=1k package=THT]
  R3 = Resistor [tolerance=±5% resistance=1k package=THT]
  High-Capacity_Transistor = NPN-Transistor [package="TO92 [THT]"]
  Heating_Pad = Resistor [tolerance=±5% resistance=2.5 package=THT]
  External_Battery_(5V) = Battery Holders [package=battery-aa-panel]
  OLED = Grove OLED 128x96

nets:
  N1: Arduino.A0, Temperature_Sensor.Vout
  N2: Arduino.D8, High-Capacity_Transistor.B
  GND: Arduino.GND, Temperature_Sensor.GND, R1.Pin_0, R2.Pin_0, R3.Pin_0, Heating_Pad.Pin_1, External_Battery_(5V).-, OLED.GND
  N3: Arduino.A4/SDA, OLED.SCL
  N4: Arduino.A5/SCL, OLED.SDA
  N5: Arduino.D5_PWM, Select_Button.Pin_3, Select_Button.Pin_4, R1.Pin_1
  N6: Arduino.D6_PWM, Up_Button.Pin_3, Up_Button.Pin_4, R2.Pin_1
  N7: Arduino.D7, Down_Button.Pin_3, Down_Button.Pin_4, R3.Pin_1
  5V: Arduino.5V, Temperature_Sensor.+Vs, Select_Button.Pin_1, Select_Button.Pin_2, Up_Button.Pin_1, Up_Button.Pin_2, Down_Button.Pin_1, Down_Button.Pin_2, OLED.VCC
  N8: High-Capacity_Transistor.E, Heating_Pad.Pin_0
  N9: High-Capacity_Transistor.C, External_Battery_(5V).+
